// Logisim project 5.1.circ as structural Verilog: 1 circuit, main circuit main
module main (
  input  S,
  input  R,
  input  [1:0] muxin,
  input  d,
  input  [3:0] Parlell_in
);

  wire clk_out, d_ff_1_q, d_ff_2_q, d_ff_3_q, d_ff_4_q, multiplexer_1_out, multiplexer_2_out,
       multiplexer_3_out, multiplexer_4_out;

  Clock clk (.out(clk_out));
  D_Flip_Flop d_ff_1 (.D(multiplexer_1_out), .clk(clk_out), .Q(d_ff_1_q), .preset(S), .reset(R));  // open: Qn
  Multiplexer #(.select(2)) multiplexer_1 (
    .in0(d_ff_1_q), .in1(d_ff_2_q), .in2(d), .in3(Parlell_in[0]), .out(multiplexer_1_out), .sel(muxin));
  D_Flip_Flop d_ff_2 (.D(multiplexer_2_out), .clk(clk_out), .Q(d_ff_2_q), .preset(S), .reset(R));  // open: Qn
  Multiplexer #(.select(2)) multiplexer_2 (
    .in0(d_ff_2_q), .in1(d_ff_3_q), .in2(d_ff_1_q), .in3(Parlell_in[1]), .out(multiplexer_2_out), .sel(muxin));
  D_Flip_Flop d_ff_3 (.D(multiplexer_3_out), .clk(clk_out), .Q(d_ff_3_q), .preset(S), .reset(R));  // open: Qn
  Multiplexer #(.select(2)) multiplexer_3 (
    .in0(d_ff_3_q), .in1(d_ff_4_q), .in2(d_ff_2_q), .in3(Parlell_in[2]), .out(multiplexer_3_out), .sel(muxin));
  D_Flip_Flop d_ff_4 (.D(multiplexer_4_out), .clk(clk_out), .Q(d_ff_4_q), .preset(S), .reset(R));  // open: Qn
  Multiplexer #(.select(2)) multiplexer_4 (
    .in0(d_ff_4_q), .in1(d), .in2(d_ff_3_q), .in3(Parlell_in[3]), .out(multiplexer_4_out), .sel(muxin));
  LED led_1 (.in(d_ff_4_q));
  LED led_2 (.in(d_ff_3_q));
  LED led_3 (.in(d_ff_2_q));
  LED led_4 (.in(d_ff_1_q));
endmodule
